// Logisim project MIPS.circ as structural Verilog: 11 circuits, main circuit main
module main (
  input  FREEZE_IN,
  input  RESET_IN,
  output IF_ERROR
);

  wire MAIN_CLOCK_out;
  wire [4:0] dec_stage_1_rd_out, dec_stage_1_rs_out, dec_stage_1_rt_out, dec_stage_1_shift_out;
  wire [5:0] dec_stage_1_func_out, dec_stage_1_opc_out;
  wire [15:0] dec_stage_1_imm_out;
  wire [31:0] dec_stage_1_vrs_out, dec_stage_1_vrt_out, if_stage_1_instruction_out,
       mem_bank_if_dec_1_instruction_out;

  Clock MAIN_CLOCK (.out(MAIN_CLOCK_out));
  IF_STAGE if_stage_1 (
    .FREEZE_IN(FREEZE_IN), .CLOCK_IN(MAIN_CLOCK_out), .RESET_IN(RESET_IN), .INST_ADDR_OVERFLOW_OUT(IF_ERROR),
    .INSTRUCTION_OUT(if_stage_1_instruction_out));
  MEM_BANK_IF_DEC mem_bank_if_dec_1 (
    .INSTRUCTION_IN(if_stage_1_instruction_out), .FREEZE_IN(FREEZE_IN), .CLOCK_IN(MAIN_CLOCK_out),
    .RESET_IN(RESET_IN), .INSTRUCTION_OUT(mem_bank_if_dec_1_instruction_out));
  DEC_STAGE dec_stage_1 (
    .INSTRUCTION_IN(mem_bank_if_dec_1_instruction_out), .FREEZE_IN(FREEZE_IN), .CLOCK_IN(MAIN_CLOCK_out),
    .RESET_IN(RESET_IN), .OPC_OUT(dec_stage_1_opc_out), .FUNC_OUT(dec_stage_1_func_out),
    .RS_OUT(dec_stage_1_rs_out), .RT_OUT(dec_stage_1_rt_out), .RD_OUT(dec_stage_1_rd_out),
    .SHIFT_OUT(dec_stage_1_shift_out), .IMM_OUT(dec_stage_1_imm_out), .VRS_OUT(dec_stage_1_vrs_out),
    .VRT_OUT(dec_stage_1_vrt_out));  // open: WRITE_EN_IN, WRITE_DATA_IN
  MEM_BANK_DEC_EXE mem_bank_dec_exe_1 (
    .OPC_IN(dec_stage_1_opc_out), .FUNC_IN(dec_stage_1_func_out), .RS_IN(dec_stage_1_rs_out),
    .RT_IN(dec_stage_1_rt_out), .RD_IN(dec_stage_1_rd_out), .SHIFT_IN(dec_stage_1_shift_out),
    .IMM_IN(dec_stage_1_imm_out), .VRS_IN(dec_stage_1_vrs_out), .VRT_IN(dec_stage_1_vrt_out));  // open: FREEZE_IN, CLOCK_IN, RESET_IN, OPC_OUT, FUNC_OUT, RS_OUT, RT_OUT, RD_OUT, SHIFT_OUT, IMM_OUT, VRS_OUT, VRT_OUT
endmodule

module _1BIT_ADD (
  input  A_IN,
  input  B_IN,
  output VAL_OUT,
  output CARRY_OUT
);

  xor xor_1 (VAL_OUT, A_IN, B_IN);
  and and_1 (CARRY_OUT, A_IN, B_IN);
endmodule

module _32BITS_ADD (
  input  [31:0] DATA_IN,
  output [31:0] DATA_OUT,
  output OVERFLOW_OUT
);

  wire n1bit_add_1_carry_out, n1bit_add_2_carry_out, n1bit_add_3_carry_out, n1bit_add_4_carry_out,
       n1bit_add_5_carry_out, n1bit_add_6_carry_out, n1bit_add_7_carry_out, n1bit_add_8_carry_out,
       n1bit_add_9_carry_out, n1bit_add_10_carry_out, n1bit_add_11_carry_out, n1bit_add_12_carry_out,
       n1bit_add_13_carry_out, n1bit_add_14_carry_out, n1bit_add_15_carry_out, n1bit_add_16_carry_out,
       n1bit_add_17_carry_out, n1bit_add_18_carry_out, n1bit_add_19_carry_out, n1bit_add_20_carry_out,
       n1bit_add_21_carry_out, n1bit_add_22_carry_out, n1bit_add_23_carry_out, n1bit_add_24_carry_out,
       n1bit_add_25_carry_out, n1bit_add_26_carry_out, n1bit_add_27_carry_out, n1bit_add_28_carry_out,
       n1bit_add_29_carry_out, n1bit_add_30_carry_out, n1bit_add_31_carry_out;

  _1BIT_ADD u_1bit_add_1 (.A_IN(1'b1), .B_IN(DATA_IN[0]), .VAL_OUT(DATA_OUT[0]), .CARRY_OUT(n1bit_add_1_carry_out));
  _1BIT_ADD u_1bit_add_2 (
    .A_IN(n1bit_add_1_carry_out), .B_IN(DATA_IN[1]), .VAL_OUT(DATA_OUT[1]), .CARRY_OUT(n1bit_add_2_carry_out));
  _1BIT_ADD u_1bit_add_3 (
    .A_IN(n1bit_add_2_carry_out), .B_IN(DATA_IN[2]), .VAL_OUT(DATA_OUT[2]), .CARRY_OUT(n1bit_add_3_carry_out));
  _1BIT_ADD u_1bit_add_4 (
    .A_IN(n1bit_add_3_carry_out), .B_IN(DATA_IN[3]), .VAL_OUT(DATA_OUT[3]), .CARRY_OUT(n1bit_add_4_carry_out));
  _1BIT_ADD u_1bit_add_5 (
    .A_IN(n1bit_add_4_carry_out), .B_IN(DATA_IN[4]), .VAL_OUT(DATA_OUT[4]), .CARRY_OUT(n1bit_add_5_carry_out));
  _1BIT_ADD u_1bit_add_6 (
    .A_IN(n1bit_add_5_carry_out), .B_IN(DATA_IN[5]), .VAL_OUT(DATA_OUT[5]), .CARRY_OUT(n1bit_add_6_carry_out));
  _1BIT_ADD u_1bit_add_7 (
    .A_IN(n1bit_add_6_carry_out), .B_IN(DATA_IN[6]), .VAL_OUT(DATA_OUT[6]), .CARRY_OUT(n1bit_add_7_carry_out));
  _1BIT_ADD u_1bit_add_8 (
    .A_IN(n1bit_add_7_carry_out), .B_IN(DATA_IN[7]), .VAL_OUT(DATA_OUT[7]), .CARRY_OUT(n1bit_add_8_carry_out));
  _1BIT_ADD u_1bit_add_9 (
    .A_IN(n1bit_add_8_carry_out), .B_IN(DATA_IN[8]), .VAL_OUT(DATA_OUT[8]), .CARRY_OUT(n1bit_add_9_carry_out));
  _1BIT_ADD u_1bit_add_10 (
    .A_IN(n1bit_add_9_carry_out), .B_IN(DATA_IN[9]), .VAL_OUT(DATA_OUT[9]), .CARRY_OUT(n1bit_add_10_carry_out));
  _1BIT_ADD u_1bit_add_11 (
    .A_IN(n1bit_add_10_carry_out), .B_IN(DATA_IN[10]), .VAL_OUT(DATA_OUT[10]),
    .CARRY_OUT(n1bit_add_11_carry_out));
  _1BIT_ADD u_1bit_add_12 (
    .A_IN(n1bit_add_11_carry_out), .B_IN(DATA_IN[11]), .VAL_OUT(DATA_OUT[11]),
    .CARRY_OUT(n1bit_add_12_carry_out));
  _1BIT_ADD u_1bit_add_13 (
    .A_IN(n1bit_add_12_carry_out), .B_IN(DATA_IN[12]), .VAL_OUT(DATA_OUT[12]),
    .CARRY_OUT(n1bit_add_13_carry_out));
  _1BIT_ADD u_1bit_add_14 (
    .A_IN(n1bit_add_13_carry_out), .B_IN(DATA_IN[13]), .VAL_OUT(DATA_OUT[13]),
    .CARRY_OUT(n1bit_add_14_carry_out));
  _1BIT_ADD u_1bit_add_15 (
    .A_IN(n1bit_add_14_carry_out), .B_IN(DATA_IN[14]), .VAL_OUT(DATA_OUT[14]),
    .CARRY_OUT(n1bit_add_15_carry_out));
  _1BIT_ADD u_1bit_add_16 (
    .A_IN(n1bit_add_15_carry_out), .B_IN(DATA_IN[15]), .VAL_OUT(DATA_OUT[15]),
    .CARRY_OUT(n1bit_add_16_carry_out));
  _1BIT_ADD u_1bit_add_17 (
    .A_IN(n1bit_add_16_carry_out), .B_IN(DATA_IN[16]), .VAL_OUT(DATA_OUT[16]),
    .CARRY_OUT(n1bit_add_17_carry_out));
  _1BIT_ADD u_1bit_add_18 (
    .A_IN(n1bit_add_17_carry_out), .B_IN(DATA_IN[17]), .VAL_OUT(DATA_OUT[17]),
    .CARRY_OUT(n1bit_add_18_carry_out));
  _1BIT_ADD u_1bit_add_19 (
    .A_IN(n1bit_add_18_carry_out), .B_IN(DATA_IN[18]), .VAL_OUT(DATA_OUT[18]),
    .CARRY_OUT(n1bit_add_19_carry_out));
  _1BIT_ADD u_1bit_add_20 (
    .A_IN(n1bit_add_19_carry_out), .B_IN(DATA_IN[19]), .VAL_OUT(DATA_OUT[19]),
    .CARRY_OUT(n1bit_add_20_carry_out));
  _1BIT_ADD u_1bit_add_21 (
    .A_IN(n1bit_add_20_carry_out), .B_IN(DATA_IN[20]), .VAL_OUT(DATA_OUT[20]),
    .CARRY_OUT(n1bit_add_21_carry_out));
  _1BIT_ADD u_1bit_add_22 (
    .A_IN(n1bit_add_21_carry_out), .B_IN(DATA_IN[21]), .VAL_OUT(DATA_OUT[21]),
    .CARRY_OUT(n1bit_add_22_carry_out));
  _1BIT_ADD u_1bit_add_23 (
    .A_IN(n1bit_add_22_carry_out), .B_IN(DATA_IN[22]), .VAL_OUT(DATA_OUT[22]),
    .CARRY_OUT(n1bit_add_23_carry_out));
  _1BIT_ADD u_1bit_add_24 (
    .A_IN(n1bit_add_23_carry_out), .B_IN(DATA_IN[23]), .VAL_OUT(DATA_OUT[23]),
    .CARRY_OUT(n1bit_add_24_carry_out));
  _1BIT_ADD u_1bit_add_25 (
    .A_IN(n1bit_add_24_carry_out), .B_IN(DATA_IN[24]), .VAL_OUT(DATA_OUT[24]),
    .CARRY_OUT(n1bit_add_25_carry_out));
  _1BIT_ADD u_1bit_add_26 (
    .A_IN(n1bit_add_25_carry_out), .B_IN(DATA_IN[25]), .VAL_OUT(DATA_OUT[25]),
    .CARRY_OUT(n1bit_add_26_carry_out));
  _1BIT_ADD u_1bit_add_27 (
    .A_IN(n1bit_add_26_carry_out), .B_IN(DATA_IN[26]), .VAL_OUT(DATA_OUT[26]),
    .CARRY_OUT(n1bit_add_27_carry_out));
  _1BIT_ADD u_1bit_add_28 (
    .A_IN(n1bit_add_27_carry_out), .B_IN(DATA_IN[27]), .VAL_OUT(DATA_OUT[27]),
    .CARRY_OUT(n1bit_add_28_carry_out));
  _1BIT_ADD u_1bit_add_29 (
    .A_IN(n1bit_add_28_carry_out), .B_IN(DATA_IN[28]), .VAL_OUT(DATA_OUT[28]),
    .CARRY_OUT(n1bit_add_29_carry_out));
  _1BIT_ADD u_1bit_add_30 (
    .A_IN(n1bit_add_29_carry_out), .B_IN(DATA_IN[29]), .VAL_OUT(DATA_OUT[29]),
    .CARRY_OUT(n1bit_add_30_carry_out));
  _1BIT_ADD u_1bit_add_31 (
    .A_IN(n1bit_add_30_carry_out), .B_IN(DATA_IN[30]), .VAL_OUT(DATA_OUT[30]),
    .CARRY_OUT(n1bit_add_31_carry_out));
  _1BIT_ADD u_1bit_add_32 (
    .A_IN(n1bit_add_31_carry_out), .B_IN(DATA_IN[31]), .VAL_OUT(DATA_OUT[31]), .CARRY_OUT(OVERFLOW_OUT));
endmodule

module _24BITS_INC (
  input  [23:0] DATA_IN,
  output [23:0] DATA_OUT,
  output OVERFLOW_OUT
);

  wire [31:0] bit_extender_1_out, n32bits_add_1_data_out;

  _32BITS_ADD u_32bits_add_1 (.DATA_IN(bit_extender_1_out), .DATA_OUT(n32bits_add_1_data_out));  // open: OVERFLOW_OUT
  assign bit_extender_1_out = {{8{1'b0}}, DATA_IN};  // Bit_Extender bit_extender_1
  and and_1 (OVERFLOW_OUT, DATA_IN[0], DATA_IN[1], DATA_IN[2], DATA_IN[3], DATA_IN[4], DATA_IN[5], DATA_IN[6], DATA_IN[7], DATA_IN[8], DATA_IN[9], DATA_IN[10], DATA_IN[11], DATA_IN[12], DATA_IN[13], DATA_IN[14], DATA_IN[15], DATA_IN[16], DATA_IN[17], DATA_IN[18], DATA_IN[19], DATA_IN[20], DATA_IN[21], DATA_IN[22], DATA_IN[23], 1'b1);
  Bit_Extender #(.in_width(32), .out_width(24)) bit_extender_2 (.in(n32bits_add_1_data_out), .out(DATA_OUT));
endmodule

module IF_STAGE (
  input  FREEZE_IN,
  input  CLOCK_IN,
  input  RESET_IN,
  output INST_ADDR_OVERFLOW_OUT,
  output [31:0] INSTRUCTION_OUT
);

  wire not_1_out, not_2_out, or_1_out;
  wire [23:0] n24bits_inc_1_data_out, register_1_q;

  or or_1 (or_1_out, INST_ADDR_OVERFLOW_OUT, RESET_IN);
  not not_1 (not_1_out, FREEZE_IN);
  _24BITS_INC u_24bits_inc_1 (
    .DATA_IN(register_1_q), .DATA_OUT(n24bits_inc_1_data_out), .OVERFLOW_OUT(INST_ADDR_OVERFLOW_OUT));
  Register #(.width(24)) register_1 (
    .D(n24bits_inc_1_data_out), .en(not_1_out), .Q(register_1_q), .clk(CLOCK_IN), .clr(or_1_out));
  not not_2 (not_2_out, FREEZE_IN);
  RAM #(.addrWidth(24), .dataWidth(32)) ram_1 (
    .addr(register_1_q), .data(INSTRUCTION_OUT), .sel(not_2_out), .clk(CLOCK_IN));  // open: ld, clr

  // Notes on the sheet:
  //   PC
endmodule

// MEM_BANK
module MEM_BANK_DEC_EXE (
  input  [5:0] OPC_IN,
  input  [5:0] FUNC_IN,
  input  [4:0] RS_IN,
  input  [4:0] RT_IN,
  input  [4:0] RD_IN,
  input  [4:0] SHIFT_IN,
  input  [15:0] IMM_IN,
  input  [31:0] VRS_IN,
  input  [31:0] VRT_IN,
  input  FREEZE_IN,
  input  CLOCK_IN,
  input  RESET_IN,
  output [5:0] OPC_OUT,
  output [5:0] FUNC_OUT,
  output [4:0] RS_OUT,
  output [4:0] RT_OUT,
  output [4:0] RD_OUT,
  output [4:0] SHIFT_OUT,
  output [15:0] IMM_OUT,
  output [31:0] VRS_OUT,
  output [31:0] VRT_OUT
);

  wire not_1_out;

  not not_1 (not_1_out, FREEZE_IN);
  Register #(.width(6)) register_1 (.D(OPC_IN), .en(not_1_out), .Q(OPC_OUT), .clk(CLOCK_IN), .clr(RESET_IN));
  Register #(.width(6)) register_2 (.D(FUNC_IN), .en(not_1_out), .Q(FUNC_OUT), .clk(CLOCK_IN), .clr(RESET_IN));
  Register #(.width(5)) register_3 (.D(RS_IN), .en(not_1_out), .Q(RS_OUT), .clk(CLOCK_IN), .clr(RESET_IN));
  Register #(.width(5)) register_4 (.D(RT_IN), .en(not_1_out), .Q(RT_OUT), .clk(CLOCK_IN), .clr(RESET_IN));
  Register #(.width(5)) register_5 (.D(RD_IN), .en(not_1_out), .Q(RD_OUT), .clk(CLOCK_IN), .clr(RESET_IN));
  Register #(.width(5)) register_6 (.D(SHIFT_IN), .en(not_1_out), .Q(SHIFT_OUT), .clk(CLOCK_IN), .clr(RESET_IN));
  Register #(.width(16)) register_7 (.D(IMM_IN), .en(not_1_out), .Q(IMM_OUT), .clk(CLOCK_IN), .clr(RESET_IN));
  Register #(.width(32)) register_8 (.D(VRS_IN), .en(not_1_out), .Q(VRS_OUT), .clk(CLOCK_IN), .clr(RESET_IN));
  Register #(.width(32)) register_9 (.D(VRT_IN), .en(not_1_out), .Q(VRT_OUT), .clk(CLOCK_IN), .clr(RESET_IN));
endmodule

module DEC_STAGE (
  input  [31:0] INSTRUCTION_IN,
  input  FREEZE_IN,
  input  CLOCK_IN,
  input  RESET_IN,
  input  WRITE_EN_IN,
  input  [31:0] WRITE_DATA_IN,
  output [5:0] OPC_OUT,
  output [5:0] FUNC_OUT,
  output [4:0] RS_OUT,
  output [4:0] RT_OUT,
  output [4:0] RD_OUT,
  output [4:0] SHIFT_OUT,
  output [15:0] IMM_OUT,
  output [31:0] VRS_OUT,
  output [31:0] VRT_OUT
);

  REGISTER_FILE register_file_1 (
    .CLOCK_IN(CLOCK_IN), .RESET_IN(RESET_IN), .WE_IN(WRITE_EN_IN), .DATA_IN(WRITE_DATA_IN),
    .ADDR_A_IN(INSTRUCTION_IN[25:21]), .ADDR_B_IN(INSTRUCTION_IN[20:16]), .FREEZE_IN(FREEZE_IN),
    .DATA_OUT(VRS_OUT), .DATA_B_OUT(VRT_OUT));

  assign FUNC_OUT = INSTRUCTION_IN[5:0];
  assign IMM_OUT = INSTRUCTION_IN[15:0];
  assign OPC_OUT = INSTRUCTION_IN[31:26];
  assign RD_OUT = INSTRUCTION_IN[15:11];
  assign RS_OUT = INSTRUCTION_IN[25:21];
  assign RT_OUT = INSTRUCTION_IN[20:16];
  assign SHIFT_OUT = INSTRUCTION_IN[10:6];

  // Notes on the sheet:
  //   SHIFT
  //   FUNC
  //   OPC
  //   RS
  //   RT
  //   RD
endmodule

// RF
module REGISTER_FILE (
  input  CLOCK_IN,
  input  RESET_IN,
  input  WE_IN,
  input  [31:0] DATA_IN,
  input  [4:0] ADDR_A_IN,
  input  [4:0] ADDR_B_IN,
  input  FREEZE_IN,
  output [31:0] DATA_OUT,
  output [31:0] DATA_B_OUT
);

  wire and_1_out, decoder_1_out1, decoder_1_out2, decoder_1_out3, decoder_1_out4, decoder_1_out5,
       decoder_1_out6, decoder_1_out7, decoder_1_out8, decoder_1_out9, decoder_1_out10, decoder_1_out11,
       decoder_1_out12, decoder_1_out13, decoder_1_out14, decoder_1_out15, decoder_1_out16, decoder_1_out17,
       decoder_1_out18, decoder_1_out19, decoder_1_out20, decoder_1_out21, decoder_1_out22, decoder_1_out23,
       decoder_1_out24, decoder_1_out25, decoder_1_out26, decoder_1_out27, decoder_1_out28, decoder_1_out29,
       decoder_1_out30, decoder_1_out31, not_1_out;
  wire [31:0] register_1_q, register_2_q, register_3_q, register_4_q, register_5_q, register_6_q,
       register_7_q, register_8_q, register_9_q, register_10_q, register_11_q, register_12_q, register_13_q,
       register_14_q, register_15_q, register_16_q, register_17_q, register_18_q, register_19_q,
       register_20_q, register_21_q, register_22_q, register_23_q, register_24_q, register_25_q,
       register_26_q, register_27_q, register_28_q, register_29_q, register_30_q, register_31_q;

  not not_1 (not_1_out, FREEZE_IN);
  and and_1 (and_1_out, WE_IN, not_1_out);
  Decoder #(.select(5), .disabled(0)) decoder_1 (
    .out1(decoder_1_out1), .out2(decoder_1_out2), .out3(decoder_1_out3), .out4(decoder_1_out4),
    .out5(decoder_1_out5), .out6(decoder_1_out6), .out7(decoder_1_out7), .out8(decoder_1_out8),
    .out9(decoder_1_out9), .out10(decoder_1_out10), .out11(decoder_1_out11), .out12(decoder_1_out12),
    .out13(decoder_1_out13), .out14(decoder_1_out14), .out15(decoder_1_out15), .out16(decoder_1_out16),
    .out17(decoder_1_out17), .out18(decoder_1_out18), .out19(decoder_1_out19), .out20(decoder_1_out20),
    .out21(decoder_1_out21), .out22(decoder_1_out22), .out23(decoder_1_out23), .out24(decoder_1_out24),
    .out25(decoder_1_out25), .out26(decoder_1_out26), .out27(decoder_1_out27), .out28(decoder_1_out28),
    .out29(decoder_1_out29), .out30(decoder_1_out30), .out31(decoder_1_out31), .sel(ADDR_A_IN), .en(and_1_out));  // open: out0
  Register #(.width(32)) register_1 (
    .D(DATA_IN), .en(decoder_1_out17), .Q(register_1_q), .clk(CLOCK_IN), .clr(RESET_IN));
  Register #(.width(32)) register_2 (
    .D(DATA_IN), .en(decoder_1_out25), .Q(register_2_q), .clk(CLOCK_IN), .clr(RESET_IN));
  Register #(.width(32)) register_3 (
    .D(DATA_IN), .en(decoder_1_out2), .Q(register_3_q), .clk(CLOCK_IN), .clr(RESET_IN));
  Register #(.width(32)) register_4 (
    .D(DATA_IN), .en(decoder_1_out1), .Q(register_4_q), .clk(CLOCK_IN), .clr(RESET_IN));
  Register #(.width(32)) register_5 (
    .D(DATA_IN), .en(decoder_1_out10), .Q(register_5_q), .clk(CLOCK_IN), .clr(RESET_IN));
  Register #(.width(32)) register_6 (
    .D(DATA_IN), .en(decoder_1_out9), .Q(register_6_q), .clk(CLOCK_IN), .clr(RESET_IN));
  Register #(.width(32)) register_7 (
    .D(DATA_IN), .en(decoder_1_out18), .Q(register_7_q), .clk(CLOCK_IN), .clr(RESET_IN));
  Register #(.width(32)) register_8 (
    .D(DATA_IN), .en(decoder_1_out26), .Q(register_8_q), .clk(CLOCK_IN), .clr(RESET_IN));
  Register #(.width(32)) register_9 (
    .D(DATA_IN), .en(decoder_1_out3), .Q(register_9_q), .clk(CLOCK_IN), .clr(RESET_IN));
  Register #(.width(32)) register_10 (
    .D(DATA_IN), .en(decoder_1_out11), .Q(register_10_q), .clk(CLOCK_IN), .clr(RESET_IN));
  Register #(.width(32)) register_11 (
    .D(DATA_IN), .en(decoder_1_out19), .Q(register_11_q), .clk(CLOCK_IN), .clr(RESET_IN));
  Register #(.width(32)) register_12 (
    .D(DATA_IN), .en(decoder_1_out27), .Q(register_12_q), .clk(CLOCK_IN), .clr(RESET_IN));
  Register #(.width(32)) register_13 (
    .D(DATA_IN), .en(decoder_1_out4), .Q(register_13_q), .clk(CLOCK_IN), .clr(RESET_IN));
  Register #(.width(32)) register_14 (
    .D(DATA_IN), .en(decoder_1_out12), .Q(register_14_q), .clk(CLOCK_IN), .clr(RESET_IN));
  Register #(.width(32)) register_15 (
    .D(DATA_IN), .en(decoder_1_out21), .Q(register_15_q), .clk(CLOCK_IN), .clr(RESET_IN));
  Register #(.width(32)) register_16 (
    .D(DATA_IN), .en(decoder_1_out20), .Q(register_16_q), .clk(CLOCK_IN), .clr(RESET_IN));
  Register #(.width(32)) register_17 (
    .D(DATA_IN), .en(decoder_1_out28), .Q(register_17_q), .clk(CLOCK_IN), .clr(RESET_IN));
  Register #(.width(32)) register_18 (
    .D(DATA_IN), .en(decoder_1_out29), .Q(register_18_q), .clk(CLOCK_IN), .clr(RESET_IN));
  Register #(.width(32)) register_19 (
    .D(DATA_IN), .en(decoder_1_out5), .Q(register_19_q), .clk(CLOCK_IN), .clr(RESET_IN));
  Register #(.width(32)) register_20 (
    .D(DATA_IN), .en(decoder_1_out6), .Q(register_20_q), .clk(CLOCK_IN), .clr(RESET_IN));
  Register #(.width(32)) register_21 (
    .D(DATA_IN), .en(decoder_1_out14), .Q(register_21_q), .clk(CLOCK_IN), .clr(RESET_IN));
  Register #(.width(32)) register_22 (
    .D(DATA_IN), .en(decoder_1_out13), .Q(register_22_q), .clk(CLOCK_IN), .clr(RESET_IN));
  Register #(.width(32)) register_23 (
    .D(DATA_IN), .en(decoder_1_out22), .Q(register_23_q), .clk(CLOCK_IN), .clr(RESET_IN));
  Register #(.width(32)) register_24 (
    .D(DATA_IN), .en(decoder_1_out30), .Q(register_24_q), .clk(CLOCK_IN), .clr(RESET_IN));
  Register #(.width(32)) register_25 (
    .D(DATA_IN), .en(decoder_1_out7), .Q(register_25_q), .clk(CLOCK_IN), .clr(RESET_IN));
  Register #(.width(32)) register_26 (
    .D(DATA_IN), .en(decoder_1_out15), .Q(register_26_q), .clk(CLOCK_IN), .clr(RESET_IN));
  Register #(.width(32)) register_27 (
    .D(DATA_IN), .en(decoder_1_out23), .Q(register_27_q), .clk(CLOCK_IN), .clr(RESET_IN));
  Register #(.width(32)) register_28 (
    .D(DATA_IN), .en(decoder_1_out31), .Q(register_28_q), .clk(CLOCK_IN), .clr(RESET_IN));
  Register #(.width(32)) register_29 (
    .D(DATA_IN), .en(decoder_1_out8), .Q(register_29_q), .clk(CLOCK_IN), .clr(RESET_IN));
  Register #(.width(32)) register_30 (
    .D(DATA_IN), .en(decoder_1_out16), .Q(register_30_q), .clk(CLOCK_IN), .clr(RESET_IN));
  Register #(.width(32)) register_31 (
    .D(DATA_IN), .en(decoder_1_out24), .Q(register_31_q), .clk(CLOCK_IN), .clr(RESET_IN));
  Multiplexer #(.select(5), .width(32), .disabled(0)) multiplexer_1 (
    .in0({32{1'b0}}), .in1(register_4_q), .in2(register_3_q), .in3(register_9_q), .in4(register_13_q),
    .in5(register_19_q), .in6(register_20_q), .in7(register_25_q), .in8(register_29_q), .in9(register_6_q),
    .in10(register_5_q), .in11(register_10_q), .in12(register_14_q), .in13(register_22_q),
    .in14(register_21_q), .in15(register_26_q), .in16(register_30_q), .in17(register_1_q),
    .in18(register_7_q), .in19(register_11_q), .in20(register_16_q), .in21(register_15_q),
    .in22(register_23_q), .in23(register_27_q), .in24(register_31_q), .in25(register_2_q),
    .in26(register_8_q), .in27(register_12_q), .in28(register_17_q), .in29(register_18_q),
    .in30(register_24_q), .in31(register_28_q), .out(DATA_OUT), .sel(ADDR_A_IN), .en(not_1_out));
  Multiplexer #(.select(5), .width(32), .disabled(0)) multiplexer_2 (
    .in0({32{1'b0}}), .in1(register_4_q), .in2(register_3_q), .in3(register_9_q), .in4(register_13_q),
    .in5(register_19_q), .in6(register_20_q), .in7(register_25_q), .in8(register_29_q), .in9(register_6_q),
    .in10(register_5_q), .in11(register_10_q), .in12(register_14_q), .in13(register_22_q),
    .in14(register_21_q), .in15(register_26_q), .in16(register_30_q), .in17(register_1_q),
    .in18(register_7_q), .in19(register_11_q), .in20(register_16_q), .in21(register_15_q),
    .in22(register_23_q), .in23(register_27_q), .in24(register_31_q), .in25(register_2_q),
    .in26(register_8_q), .in27(register_12_q), .in28(register_17_q), .in29(register_18_q),
    .in30(register_24_q), .in31(register_28_q), .out(DATA_B_OUT), .sel(ADDR_B_IN), .en(not_1_out));

  // Notes on the sheet:
  //   R1-R8
  //   R9-R16
  //   R25-R31
  //   R17-R24
endmodule

module L1I_CACHE (
  input  [23:0] ADDR_IN,
  input  FREEZE_IN,
  input  CLOCK_IN,
  input  RESET_IN
);

  RAM #(.addrWidth(24), .dataWidth(32)) ram_1 ();  // open: addr, data, sel, clk, ld, clr

  // Notes on the sheet:
  //   TAG
  //   BYTE
  //   OFFSET
  //   INDEX
endmodule

module VALID_VECTOR_250_LINES (
  input  [7:0] LINE_INDEX_IN,
  input  CLOCK_IN,
  input  RESET_IN,
  input  SET_IN,
  input  CLEAR_IN,
  output VALID_OUT
);

  wire controlled_buffer_1_out, not_1_out, or_1_out, or_2_out, ram_1_data;

  assign controlled_buffer_1_out = or_2_out ? or_1_out : 1'bz;  // Controlled_Buffer controlled_buffer_1
  or or_1 (or_1_out, SET_IN, ~CLEAR_IN);  // OR_Gate
  or or_2 (or_2_out, SET_IN, CLEAR_IN);
  RAM #(.dataWidth(1), .bus("separate")) ram_1 (
    .addr(LINE_INDEX_IN), .din(controlled_buffer_1_out), .data(ram_1_data), .str(or_2_out), .sel(1'b1),
    .clk(CLOCK_IN), .ld(not_1_out), .clr(RESET_IN));
  not not_1 (not_1_out, or_2_out);
  assign VALID_OUT = not_1_out ? ram_1_data : 1'bz;  // Controlled_Buffer controlled_buffer_2
endmodule

// IF_DEC_MEM
module MEM_BANK_IF_DEC (
  input  [31:0] INSTRUCTION_IN,
  input  FREEZE_IN,
  input  CLOCK_IN,
  input  RESET_IN,
  output [31:0] INSTRUCTION_OUT
);

  wire not_1_out;

  not not_1 (not_1_out, FREEZE_IN);
  Register #(.width(32)) register_1 (
    .D(INSTRUCTION_IN), .en(not_1_out), .Q(INSTRUCTION_OUT), .clk(CLOCK_IN), .clr(RESET_IN));
endmodule
